// Logisim project hack.circ as structural Verilog
module alu (
  input  [15:0] x,
  input  [15:0] o,
  input  [15:0] y,
  input  zx,
  input  nx,
  input  zy,
  input  ny,
  input  f,
  input  no,
  output ng,
  output zr
);

  wire [15:0] multiplexer_1_out, multiplexer_2_out, multiplexer_3_out, multiplexer_4_out, not_1_out,
       not_2_out;

  Multiplexer #(.width(16)) multiplexer_1 (.in0(x), .in1({16{1'b0}}), .out(multiplexer_1_out), .sel(zx));
  Multiplexer #(.width(16)) multiplexer_2 (.in0(y), .in1({16{1'b0}}), .out(multiplexer_2_out), .sel(zy));
  assign not_1_out = ~multiplexer_1_out;  // NOT_Gate not_1, 16 bits wide
  Multiplexer #(.width(16)) multiplexer_3 (.in0(multiplexer_2_out), .in1(not_2_out), .out(multiplexer_3_out), .sel(ny));
  assign not_2_out = ~multiplexer_2_out;  // NOT_Gate not_2, 16 bits wide
  Multiplexer #(.width(16)) multiplexer_4 (.in0(multiplexer_1_out), .in1(not_1_out), .out(multiplexer_4_out), .sel(nx));
endmodule
